# Fritzing sketch charge_monitor (saved by Fritzing 0.9.2b)
perfboards: 1

parts:
  D1 = SOLAR-IXYS [package=solarbit-12x1]
  J2 = shrouded pin header, 14 pins [form="♂ (shrouded male)"]
  J3 = female pin header, 7 pins [form="♀ (female)"]
  J4 = female pin header, 7 pins [form="♀ (female)"]
  R1 = Resistor [tolerance=±5% resistance=3.3M package=THT]
  R2 = Resistor [tolerance=±5% resistance=3.3M package=THT]
  LF1 = LF353 FET Dual OpAmp [package="DIP8 [THT]"]
  J5 = female pin header, 2 pins [form="♀ (female)"]
  J6 = female pin header, 2 pins [form="♀ (female)"]
  Part1 = Arduino Nano (Rev3.0)
  R3 = Resistor [tolerance=±5% resistance=68 package=THT]
  C2_25F_Supercap = Electrolytic Capacitor [package="200 mil [THT, electrolytic]"]
  R4_Simulated_Load_70mW = Resistor [tolerance=±5% resistance=390 package=THT]
  C1 = Ceramic Capacitor [capacitance=100nF package="100 mil [THT, multilayer]"]

nets:
  N1: D1.A, R1.Pin_0, R3.Pin_1
  N2: D1.C, J2.pin5, J4.pin5, R2.Pin_0, LF1.connector3, J5.pin2, Part1.GND, C2_25F_Supercap.-, R4_Simulated_Load_70mW.Pin_1, C1.1
  3v3: J2.pin14, J3.pin1, LF1.connector4, R4_Simulated_Load_70mW.Pin_0
  N3: R1.Pin_1, R2.Pin_1, LF1.connector2
  N4: LF1.connector0, LF1.connector1, J6.pin1, Part1.A0
  N5: LF1.connector5, LF1.connector6, J6.pin2, Part1.A1
  N6: LF1.connector7, J5.pin1, Part1.5V, C1.0
  N7: R3.Pin_0, C2_25F_Supercap.+

notes:
  LEOSTICK

custom parts:
  LF353 FET Dual OpAmp: Dual FET-input OpAmp
  Electrolytic Capacitor: electrolytic capacitor
