# Fritzing sketch esp01-simple_temp (saved by Fritzing 0.9.2b)
circuit board: 8.46667cm x 5.64444cm
breadboards: 1

parts:
  R1 = Resistor [tolerance=±5% resistance=4.7k package=THT]
  S1 = Pushbutton [package=THT]
  R2 = Resistor [tolerance=±5% resistance=4.7k package=THT]
  S2 = Toggle Switch [package=THT]
  LED1 = LED - 3mm [color="Red (633nm)" package="3 mm [THT]"]
  J1 = female pin header, 2 pins [form="♀ (female)"]
  J2 = female pin header, 2 pins [form="♀ (female)"]
  F2 = Resettable Fuse PTC [package=ptc]
  U1 = ESP8266 WiFi Module [part_number=ESP8266]
  R3 = Resistor [tolerance=±5% resistance=3.3k package="1206 [SMD]"]
  R4 = Resistor [tolerance=±5% resistance=3.3k package="1206 [SMD]"]
  LED2 = LED - 3mm [color="Yellow (595nm)" package="3 mm [THT]"]
  T1 = DS18B20 [package="TO92 [THT]"]

nets:
  3.3V: R1.Pin_0, R2.Pin_0, LED1.anode, J2.pin1, U1.VCC, T1.+Vs
  N1: R1.Pin_1, U1.CH_PD
  N2: S1.leg0, R2.Pin_1, U1.RESET
  GND: S1.leg1, J2.pin2, F2.1, U1.GND, R4.Pin_1, T1.GND
  N3: S2.L1, F2.2
  N4: S2.COM, U1.GPIO_0, R3.Pin_0
  N5: S2.L2, LED2.anode
  N6: LED1.cathode, R3.Pin_1
  N7: J1.pin1, U1.RXD
  N8: J1.pin2, U1.TXD
  N9: U1.GPIO_2, T1.Vout
  N10: R4.Pin_0, LED2.cathode

custom parts:
  ESP8266 WiFi Module: Generic WiFi Module based on the ESP8266 with onboard PCB antenna and UART communications
