# Fritzing sketch esp01-ground-sensor-prototype0-threshold (saved by Fritzing 0.9.2b)
breadboards: 1

parts:
  D2 = SOLAR-IXYS [package=solarbit-12x1]
  J3 = shrouded pin header, 14 pins [form="♂ (shrouded male)"]
  C2_25F = Electrolytic Capacitor [package="200 mil [THT, electrolytic]"]
  D3 = Schottky Diode [part_number=1N5817 package="Melf DO-213 AB [SMD]"]
  U1 = Voltage Regulator - 3.3V [package="TO220 [THT]"]
  R1 = Resistor [tolerance=±5% resistance=4.7k package=THT]
  R2 = Resistor [tolerance=±5% resistance=4.7k package=THT]
  U2 = ESP8266 WiFi Module [part_number=ESP8266]
  RESET = Pushbutton [package=THT]
  T1 = DS18B20 [package="TO92 [THT]"]
  Program = Pushbutton [package=THT]
  T2 = DS18B20 [package="TO92 [THT]"]
  R3 = Resistor [tolerance=±5% resistance=10 package=THT]
  Bypass = Pushbutton [package=THT]
  R5 = Resistor [tolerance=±5% resistance=4.7k package=THT]
  R6 = Resistor [tolerance=±5% resistance=4.7k package=THT]

nets:
  GND: D2.A, J3.pin12, C2_25F.-, U1.GND, U2.GND, RESET.leg0, T1.GND, Program.leg0, T2.GND, Bypass.leg0
  N1: D2.C, J3.pin2, D3.anode
  3.3V: J3.pin7, U1.output_voltage, R1.Pin_1, R2.Pin_0, U2.VCC, T1.+Vs, T2.+Vs, R5.Pin_1, R6.Pin_1
  N2: C2_25F.+, R3.Pin_1
  N3: D3.cathode, U1.input_voltage, R3.Pin_0
  N4: R1.Pin_0, U2.RESET, RESET.leg1
  N5: R2.Pin_1, U2.CH_PD
  N6: U2.GPIO_0, T1.Vout, Program.leg1, T2.Vout, R5.Pin_0
  N7: U2.GPIO_2, Bypass.leg1, R6.Pin_0

notes:
  CH_PD connected to SOC pin 8 (XPD_DCDC) to enable Deep Sleep.
  Next version will use ESP-07!

custom parts:
  Electrolytic Capacitor: electrolytic capacitor
  ESP8266 WiFi Module: Generic WiFi Module based on the ESP8266 with onboard PCB antenna and UART communications
